# Fritzing sketch scheme (saved by Fritzing 0.9.3b)
breadboards: 1

parts:
  part = Arduino Leonardo (Rev3b)
  part_2 = Arduino Yun
  C2 = Ceramic Capacitor [capacitance=10µF package="100 mil [THT, multilayer]"]
  C1 = Ceramic Capacitor [capacitance=10µF package="100 mil [THT, multilayer]"]
  R3 = Rotary Potentiometer (Small) [maximum_resistance=100kΩ package=THT]
  R2 = Resistor [tolerance=±5% resistance=5.1k package=THT]
  R1 = Resistor [tolerance=±5% resistance=5.1k package=THT]

nets:
  N1: part.D5_PWM, R1.Pin_0
  N2: part.A0, part_2.A0, R3.leg2
  N3: part.A1, C2.1, R2.Pin_1
  N4: part_2.A1, C1.1, R1.Pin_1
  N5: part_2.D5_PWM, R2.Pin_0
  N6: part_2.ioref, R3.leg1
  GND: C2.0, C1.0, R3.wiper
